# Fritzing sketch Secuencia led (saved by Fritzing 0.9.3b)
breadboards: 1

parts:
  CD4017 = IC, DIP package, 16 pins [chip_label=CD4017]
  555 = IC, DIP package, 8 pins [chip_label=555]
  R1 = Resistor [tolerance=±5% resistance=1k package=THT]
  C1 = Electrolytic Capacitor [capacitance=10µF package="100 mil [THT, electrolytic]"]
  R2 = Rotary Potentiometer (Small) [maximum_resistance=10kΩ package=THT]
  R3 = Resistor [tolerance=±5% resistance=1k package=THT]
  LED1 = LED - 5mm [color="Red (633nm)" package="5 mm [THT]"]

nets:
  N1: CD4017.pin14, 555.pin3, LED1.anode
  N2: 555.pin1, C1.-, R3.Pin_1
  N3: 555.pin2, 555.pin6, C1.+, R2.wiper
  N4: 555.pin4, 555.pin8, R1.Pin_0
  N5: 555.pin7, R1.Pin_1, R2.leg1
  N6: R3.Pin_0, LED1.cathode
